# Fritzing sketch WiringDiagramForObstacalOvidingCar (saved by Fritzing 0.9.3b)
breadboards: 2

parts:
  Part1 = Arduino Ethernet Shield (Rev3)
  IC1 = L293D [package=THT]
  VCC1 = 4 x AAA Battery Mount
  M1 = DC Motor
  M2 = DC Motor
  M3 = DC Motor
  M5 = DC Motor
  hc-sr1 = hc-sr04

nets:
  5V: Part1.5V, IC1.+Vmotor, IC1.+V, VCC1.+, hc-sr1.VCC
  N1: Part1.D2, IC1.In_1
  N2: Part1.PWM_D3, IC1.In_2
  N3: Part1.SDCS, IC1.In_3
  N4: Part1.PWM_D5, IC1.In_4
  N5: Part1.PWM_D6, hc-sr1.Trig
  N6: Part1.D7, hc-sr1.Echo
  GND: Part1.GND, IC1.0V, VCC1.-, hc-sr1.GND
  N7: IC1.Out_1_(_Controlled_by_Enable_1_), M1.pin_2, M2.pin_2
  N8: IC1.Out_2_(_Controlled_by_Enable_1_), M1.pin_1, M2.pin_1
  N9: IC1.Out_3_(_Controlled_by_Enable_2_), M3.pin_1, M5.pin_1
  N10: IC1.Out_4_(_Controlled_by_Enable_2_), M3.pin_2, M5.pin_2
